// Logisim project Nycksandro_Lima_8bits .circ as structural Verilog: 16 circuits, main circuit main
module main (
  output [7:0] out_1
);

  wire and_1_out, comparator_1_eq, comparator_2_eq, D_A, flags_out_6, flags_out_7, flags_out_8, flags_out_9,
       I_O, IO_E, IO_S, keyboard_1_avail, or_1_out, register_1_q, register_2_q, t_ff_1_q, uc_1_init,
       uc_1_ir_set, uc_1_to_acc_e, uc_1_to_acc_s, uc_1_to_bus1, uc_1_to_flag_s, uc_1_to_iar_e, uc_1_to_iar_s,
       uc_1_to_mar_s, uc_1_to_r0_e, uc_1_to_r0_s, uc_1_to_r1_e, uc_1_to_r1_s, uc_1_to_r2_e, uc_1_to_r2_s,
       uc_1_to_r3_e, uc_1_to_r3_s, uc_1_to_ram_e, uc_1_to_ram_s, uc_1_to_tmp_s, ula_1_a_igual_b,
       ula_1_a_maior, ula_1_carry_out, ula_1_zero;
  wire [2:0] uc_1_ula_op;
  wire [6:0] bit_extender_2_out, keyboard_1_data;
  wire [7:0] ACC_q, b1_out_3, bit_extender_1_out, controlled_buffer_1_out, IAR_q, IR_q, MAR_q, R0_q, R1_q,
       R2_q, R3_q, TMP_q, ula_1_op_logic;

  ULA ula_1 (
    .A(controlled_buffer_1_out), .B(b1_out_3), .Op_logic(ula_1_op_logic), .op_ULA(uc_1_ula_op),
    .carry_out(ula_1_carry_out), .a_maior(ula_1_a_maior), .a_igual_b(ula_1_a_igual_b), .zero(ula_1_zero));
  Comparator comparator_1 (.a(controlled_buffer_1_out), .b(8'h97), .eq(comparator_1_eq));  // open: gt, lt
  Register TMP (.D(controlled_buffer_1_out), .Q(TMP_q), .clk(uc_1_to_tmp_s));  // open: en, clr
  bus_1 b1 (.in_1(TMP_q), .out_3(b1_out_3), .in_2(uc_1_to_bus1));
  flag flags (
    .in_1(ula_1_carry_out), .in_2(ula_1_a_maior), .in_3(ula_1_a_igual_b), .in_4(ula_1_zero),
    .in_5(uc_1_to_flag_s), .out_6(flags_out_6), .out_7(flags_out_7), .out_8(flags_out_8), .out_9(flags_out_9));
  Register ACC (.D(ula_1_op_logic), .Q(ACC_q), .clk(uc_1_to_acc_s));  // open: en, clr
  assign controlled_buffer_1_out = uc_1_to_acc_e ? ACC_q : 8'bz;  // Controlled_Buffer controlled_buffer_1
  T_Flip_Flop t_ff_1 (.clk(IO_E), .T(keyboard_1_avail), .Q(t_ff_1_q));  // open: Qn, preset, reset
  Register #(.width(1)) register_1 (.D(comparator_1_eq), .Q(register_1_q), .clk(and_1_out));  // open: en, clr
  and and_1 (and_1_out, IO_S, D_A, I_O);
  Keyboard #(.trigger("falling")) keyboard_1 (
    .clk(t_ff_1_q), .re(register_1_q), .avail(keyboard_1_avail), .data(keyboard_1_data));  // open: clr
  // Probe on controlled_buffer_1_out
  assign controlled_buffer_1_out = uc_1_to_r0_e ? R0_q : 8'bz;  // Controlled_Buffer controlled_buffer_2
  Register R0 (.D(controlled_buffer_1_out), .Q(R0_q), .clk(uc_1_to_r0_s));  // open: en, clr
  assign bit_extender_1_out = {{1{1'b0}}, keyboard_1_data};  // Bit_Extender bit_extender_1
  assign controlled_buffer_1_out = IO_E ? bit_extender_1_out : 8'bz;  // Controlled_Buffer controlled_buffer_3
  assign controlled_buffer_1_out = uc_1_to_r1_e ? R1_q : 8'bz;  // Controlled_Buffer controlled_buffer_4
  Register R1 (.D(controlled_buffer_1_out), .Q(R1_q), .clk(uc_1_to_r1_s));  // open: en, clr
  Register IAR (.D(controlled_buffer_1_out), .Q(IAR_q), .clk(uc_1_to_iar_s));  // open: en, clr
  Register R2 (.D(controlled_buffer_1_out), .Q(R2_q), .clk(uc_1_to_r2_s));  // open: en, clr
  assign controlled_buffer_1_out = uc_1_to_iar_e ? IAR_q : 8'bz;  // Controlled_Buffer controlled_buffer_5
  Comparator comparator_2 (.a(controlled_buffer_1_out), .b(8'h98), .eq(comparator_2_eq));  // open: gt, lt
  assign controlled_buffer_1_out = uc_1_to_r2_e ? R2_q : 8'bz;  // Controlled_Buffer controlled_buffer_6
  UC uc_1 (
    .ULA_op(uc_1_ula_op), .from_carry_out(flags_out_6), .from_larger(flags_out_7), .from_equal(flags_out_8),
    .from_zero(flags_out_9), .to_flag_s(uc_1_to_flag_s), .to_bus1(uc_1_to_bus1), .to_TMP_s(uc_1_to_tmp_s),
    .to_R0_s(uc_1_to_r0_s), .to_R0_e(uc_1_to_r0_e), .to_R1_s(uc_1_to_r1_s), .to_R1_e(uc_1_to_r1_e),
    .to_R2_s(uc_1_to_r2_s), .to_R2_e(uc_1_to_r2_e), .to_R3_s(uc_1_to_r3_s), .to_R3_e(uc_1_to_r3_e),
    .to_MAR_s(uc_1_to_mar_s), .to_ACC_s(uc_1_to_acc_s), .to_ACC_e(uc_1_to_acc_e), .to_IAR_s(uc_1_to_iar_s),
    .to_IAR_e(uc_1_to_iar_e), .IR_input(IR_q), .IR_set(uc_1_ir_set), .Input_Output(I_O), .Data_Adress(D_A),
    .to_IO_e(IO_E), .to_IO_s(IO_S), .to_RAM_s(uc_1_to_ram_s), .to_RAM_e(uc_1_to_ram_e), .init(uc_1_init));
  LED led_1 (.in(uc_1_init));
  Register IR (.D(controlled_buffer_1_out), .Q(IR_q), .clk(uc_1_ir_set));  // open: en, clr
  Register #(.width(1)) register_2 (.D(comparator_2_eq), .Q(register_2_q), .clk(and_1_out));  // open: en, clr
  Register R3 (.D(controlled_buffer_1_out), .Q(R3_q), .clk(uc_1_to_r3_s));  // open: en, clr
  Bit_Extender #(.out_width(7), .\type ("zero")) bit_extender_2 (
    .in(controlled_buffer_1_out), .out(bit_extender_2_out));
  TTY tty_1 (.data(bit_extender_2_out), .clk(IO_S), .we(register_2_q));  // open: clr
  assign controlled_buffer_1_out = uc_1_to_r3_e ? R3_q : 8'bz;  // Controlled_Buffer controlled_buffer_7
  Register MAR (.D(controlled_buffer_1_out), .Q(MAR_q), .clk(uc_1_to_mar_s));  // open: en, clr
  or or_1 (or_1_out, uc_1_to_ram_s, uc_1_to_ram_e);
  RAM #(.\type ("nonvolatile")) ram_1 (
    .addr(MAR_q), .we(uc_1_to_ram_s), .oe(uc_1_to_ram_e), .clk(or_1_out), .din(controlled_buffer_1_out),
    .dout(out_1));
  assign controlled_buffer_1_out = uc_1_to_ram_e ? out_1 : 8'bz;  // Controlled_Buffer controlled_buffer_8
endmodule

module somador_1bit (
  input  c_in,
  input  A,
  input  B,
  output saida,
  output c_out
);

  wire and_1_out, and_2_out, and_3_out, xor_1_out;

  xor xor_1 (xor_1_out, A, B);
  and and_1 (and_1_out, A, c_in);
  and and_2 (and_2_out, A, B);
  and and_3 (and_3_out, B, c_in);
  xor xor_2 (saida, xor_1_out, c_in);
  or or_1 (c_out, and_1_out, and_2_out, and_3_out);
endmodule

module somador_8bits (
  input  \const ,
  input  [7:0] a,
  input  [7:0] b,
  output [7:0] saida,
  output c_out
);

  wire somador_1bit_1_c_out, somador_1bit_2_c_out, somador_1bit_3_c_out, somador_1bit_4_c_out,
       somador_1bit_5_c_out, somador_1bit_6_c_out, somador_1bit_7_c_out;

  somador_1bit somador_1bit_1 (.A(a[0]), .B(b[0]), .c_in(\const ), .c_out(somador_1bit_1_c_out), .saida(saida[0]));
  somador_1bit somador_1bit_2 (
    .A(a[1]), .B(b[1]), .c_in(somador_1bit_1_c_out), .c_out(somador_1bit_2_c_out), .saida(saida[1]));
  somador_1bit somador_1bit_3 (
    .A(a[2]), .B(b[2]), .c_in(somador_1bit_2_c_out), .c_out(somador_1bit_3_c_out), .saida(saida[2]));
  somador_1bit somador_1bit_4 (
    .A(a[3]), .B(b[3]), .c_in(somador_1bit_3_c_out), .c_out(somador_1bit_4_c_out), .saida(saida[3]));
  somador_1bit somador_1bit_5 (
    .A(a[4]), .B(b[4]), .c_in(somador_1bit_4_c_out), .c_out(somador_1bit_5_c_out), .saida(saida[4]));
  somador_1bit somador_1bit_6 (
    .A(a[5]), .B(b[5]), .c_in(somador_1bit_5_c_out), .c_out(somador_1bit_6_c_out), .saida(saida[5]));
  somador_1bit somador_1bit_7 (
    .A(a[6]), .B(b[6]), .c_in(somador_1bit_6_c_out), .c_out(somador_1bit_7_c_out), .saida(saida[6]));
  somador_1bit somador_1bit_8 (.A(a[7]), .B(b[7]), .c_in(somador_1bit_7_c_out), .c_out(c_out), .saida(saida[7]));
endmodule

module mem_1bit (
  input  in_1,
  input  in_2,
  output out_3
);

  wire nand_1_out, nand_2_out, nand_4_out;

  nand nand_1 (nand_1_out, in_1, in_2);
  // Probe on nand_1_out
  nand nand_2 (nand_2_out, nand_1_out, in_2);
  nand nand_3 (out_3, nand_1_out, nand_4_out);
  nand nand_4 (nand_4_out, out_3, nand_2_out);
endmodule

module registrador (
  input  [7:0] in_1,
  input  in_2,
  input  in_3,
  output [7:0] out_4
);

  wire mem_1bit_1_out_3, mem_1bit_2_out_3, mem_1bit_3_out_3, mem_1bit_4_out_3, mem_1bit_5_out_3,
       mem_1bit_6_out_3, mem_1bit_7_out_3, mem_1bit_8_out_3;

  mem_1bit mem_1bit_1 (.in_1(in_1[0]), .in_2(in_2), .out_3(mem_1bit_1_out_3));
  mem_1bit mem_1bit_2 (.in_1(in_1[1]), .in_2(in_2), .out_3(mem_1bit_2_out_3));
  mem_1bit mem_1bit_3 (.in_1(in_1[2]), .in_2(in_2), .out_3(mem_1bit_3_out_3));
  mem_1bit mem_1bit_4 (.in_1(in_1[3]), .in_2(in_2), .out_3(mem_1bit_4_out_3));
  mem_1bit mem_1bit_5 (.in_1(in_1[4]), .in_2(in_2), .out_3(mem_1bit_5_out_3));
  mem_1bit mem_1bit_6 (.in_1(in_1[5]), .in_2(in_2), .out_3(mem_1bit_6_out_3));
  mem_1bit mem_1bit_7 (.in_1(in_1[6]), .in_2(in_2), .out_3(mem_1bit_7_out_3));
  mem_1bit mem_1bit_8 (.in_1(in_1[7]), .in_2(in_2), .out_3(mem_1bit_8_out_3));
  and and_1 (out_4[0], mem_1bit_1_out_3, in_3);
  and and_2 (out_4[1], mem_1bit_2_out_3, in_3);
  and and_3 (out_4[2], mem_1bit_3_out_3, in_3);
  and and_4 (out_4[3], mem_1bit_4_out_3, in_3);
  and and_5 (out_4[4], mem_1bit_5_out_3, in_3);
  and and_6 (out_4[5], mem_1bit_6_out_3, in_3);
  and and_7 (out_4[6], mem_1bit_7_out_3, in_3);
  and and_8 (out_4[7], mem_1bit_8_out_3, in_3);
endmodule

module SHL (
  input  c_in,
  input  [7:0] in_2,
  output [7:0] out_3,
  output c_out
);


  assign c_out = in_2[7];
  assign out_3 = {in_2[6:0], c_in};
endmodule

module ULA (
  input  [2:0] op_ULA,
  input  [7:0] A,
  input  [7:0] B,
  output carry_out,
  output [7:0] Op_logic,
  output a_maior,
  output a_igual_b,
  output zero
);

  wire adder_1_cout, or_2_out, Sleft_c_out, Sright_c_out;
  wire [7:0] adder_1_out, and_1_out, not_1_out, or_1_out, Sleft_out_3, Sright_out_4, xor_1_out;

  SHR Sright (.in_1(A), .c_out(Sright_c_out), .out_4(Sright_out_4));  // open: c_in
  SHL Sleft (.in_2(A), .c_out(Sleft_c_out), .out_3(Sleft_out_3));  // open: c_in
  assign not_1_out = ~A;  // NOT_Gate not_1, 8 bits wide
  Comparator comparator_1 (.a(A), .b(B), .gt(a_maior), .eq(a_igual_b));  // open: lt
  Adder adder_1 (.a(A), .b(B), .out(adder_1_out), .cin(1'b0), .cout(adder_1_cout));
  assign and_1_out = A & B;  // AND_Gate and_1, 8 bits wide
  assign or_1_out = A | B;  // OR_Gate or_1, 8 bits wide
  assign xor_1_out = A ^ B;  // XOR_Gate xor_1, 8 bits wide
  Multiplexer #(.select(3), .width(8)) multiplexer_1 (
    .in0(adder_1_out), .in1(Sright_out_4), .in2(Sleft_out_3), .in3(not_1_out), .in4(and_1_out),
    .in5(or_1_out), .in6(xor_1_out), .in7(A), .out(Op_logic), .sel(op_ULA));
  Multiplexer #(.select(3)) multiplexer_2 (
    .in0(adder_1_cout), .in1(Sright_c_out), .in2(Sleft_c_out), .in3(1'b0), .in4(1'b0), .in5(1'b0),
    .in6(1'b0), .in7(1'b0), .out(carry_out), .sel(op_ULA));
  or or_2 (or_2_out, Op_logic[0], Op_logic[1], Op_logic[2], Op_logic[3], Op_logic[4], Op_logic[5], Op_logic[6], Op_logic[7]);
  not not_2 (zero, or_2_out);

  // Notes on the sheet:
  //   NOT
  //   AND
  //   OR
  //   XOR
endmodule

module SHR (
  input  [7:0] in_1,
  input  c_in,
  output c_out,
  output [7:0] out_4
);


  assign c_out = in_1[0];
  assign out_4 = {c_in, in_1[7:1]};
endmodule

module cl0ck (
  output clk_s,
  output out_2,
  output clk_e
);

  wire clk_d_out;

  Clock #(.highDuration(2), .lowDuration(2)) main_clk (.out(out_2));
  Clock #(.highDuration(2), .lowDuration(2), .phaseOffset(3)) clk_d (.out(clk_d_out));
  and and_1 (clk_s, clk_d_out, out_2);
  or or_1 (clk_e, out_2, clk_d_out);
endmodule

module stepper (
  input  in_1,
  output out_2,
  output p1,
  output p2,
  output p3,
  output p4,
  output p5,
  output p6
);

  wire decoder_1_out7;
  wire [2:0] counter_1_q;

  Counter #(.max('h7), .width(3)) counter_1 (
    .D(3'b000), .Q(counter_1_q), .clk(in_1), .clr(decoder_1_out7));  // open: load, count, carry, up
  Decoder #(.enable("false"), .select(3)) decoder_1 (
    .out0(out_2), .out1(p1), .out2(p2), .out3(p3), .out4(p4), .out5(p5), .out6(p6), .out7(decoder_1_out7),
    .sel(counter_1_q));
endmodule

module UC (
  input  from_carry_out,
  input  from_larger,
  input  from_equal,
  input  from_zero,
  input  [7:0] IR_input,
  output to_bus1,
  output to_TMP_s,
  output to_R0_s,
  output to_R0_e,
  output to_R1_s,
  output to_R1_e,
  output to_R2_s,
  output to_R2_e,
  output to_R3_s,
  output to_R3_e,
  output to_MAR_s,
  output to_RAM_s,
  output [2:0] ULA_op,
  output to_RAM_e,
  output init,
  output to_flag_s,
  output to_ACC_s,
  output to_ACC_e,
  output to_IAR_s,
  output to_IAR_e,
  output IR_set,
  output Input_Output,
  output Data_Adress,
  output to_IO_e,
  output to_IO_s
);

  wire A_out, and_8_out, and_9_out, and_10_out, and_11_out, and_12_out, and_13_out, and_14_out, and_15_out,
       and_16_out, and_17_out, and_18_out, and_19_out, and_20_out, and_21_out, and_22_out, and_23_out,
       and_24_out, and_25_out, and_26_out, and_27_out, C_out, clk_e, clk_s, clocks_out_2,
       decoder_3x8_uc_1_out_5, decoder_3x8_uc_1_out_6, decoder_3x8_uc_1_out_7, decoder_3x8_uc_1_out_8,
       decoder_3x8_uc_1_out_9, decoder_3x8_uc_1_out_10, decoder_3x8_uc_1_out_11, decoder_3x8_uc_1_out_12,
       decoder_3x8_uc_1_out_13, E_out, not_1_out, not_2_out, or_1_out, or_3_out, or_4_out, or_5_out,
       or_6_out, or_7_out, or_8_out, or_9_out, or_10_out, Ra_out, Rb_out, s_1, s_2, s_3, s_4, s_5, s_6, Z_out;

  cl0ck clocks (.clk_s(clk_s), .out_2(clocks_out_2), .clk_e(clk_e));
  and and_1 (to_IAR_e, or_3_out, clk_e);
  and and_2 (to_RAM_e, or_1_out, clk_e);
  and and_3 (to_ACC_e, or_4_out, clk_e);
  and and_4 (to_IO_e, and_24_out, clk_e);
  or or_1 (or_1_out, s_2, and_27_out, and_22_out, and_21_out, and_19_out);
  dec4x8_UC dec4x8_uc_1 (
    .out_8(to_R0_e), .out_9(to_R1_e), .out_10(to_R2_e), .out_11(to_R3_e), .in_1(clk_e), .in_2(Rb_out),
    .in_3(Ra_out), .in_4(IR_input[0]), .in_5(IR_input[1]), .in_6(IR_input[2]), .in_7(IR_input[3]));
  or or_2 (to_bus1, s_1, and_15_out, and_14_out, and_11_out);
  or or_3 (or_3_out, s_1, and_11_out, and_13_out, and_14_out);
  or or_4 (or_4_out, s_3, and_23_out, and_26_out, and_25_out);
  or Rb (Rb_out, and_8_out, and_20_out, and_12_out, and_16_out);
  or Ra (Ra_out, and_10_out, and_9_out, and_18_out);
  and and_5 (ULA_op[0], s_5, IR_input[7], IR_input[4]);
  and and_6 (ULA_op[1], s_5, IR_input[7], IR_input[5]);
  and and_7 (ULA_op[2], s_5, IR_input[7], IR_input[6]);
  decoder_3x8_UC decoder_3x8_uc_1 (
    .out_5(decoder_3x8_uc_1_out_5), .b7(IR_input[7]), .b6(IR_input[6]), .b5(IR_input[5]), .b4(IR_input[4]),
    .out_6(decoder_3x8_uc_1_out_6), .out_7(decoder_3x8_uc_1_out_7), .out_8(decoder_3x8_uc_1_out_8),
    .out_9(decoder_3x8_uc_1_out_9), .out_10(decoder_3x8_uc_1_out_10), .out_11(decoder_3x8_uc_1_out_11),
    .out_12(decoder_3x8_uc_1_out_12), .out_13(decoder_3x8_uc_1_out_13));
  stepper stepper_1 (.in_1(clocks_out_2), .p1(s_1), .p2(s_2), .p3(s_3), .p4(s_4), .p5(s_5), .p6(s_6), .out_2(init));
  and and_8 (and_8_out, s_4, decoder_3x8_uc_1_out_5);
  and and_9 (and_9_out, s_4, decoder_3x8_uc_1_out_6);
  and and_10 (and_10_out, s_4, decoder_3x8_uc_1_out_7);
  and and_11 (and_11_out, s_4, decoder_3x8_uc_1_out_8);
  and and_12 (and_12_out, s_4, decoder_3x8_uc_1_out_9);
  and and_13 (and_13_out, s_4, decoder_3x8_uc_1_out_10);
  and and_14 (and_14_out, s_4, decoder_3x8_uc_1_out_11);
  and and_15 (and_15_out, s_4, decoder_3x8_uc_1_out_12);
  and and_16 (and_16_out, s_4, decoder_3x8_uc_1_out_13, IR_input[3]);
  and C (C_out, IR_input[3], from_carry_out);
  and A (A_out, IR_input[2], from_larger);
  and E (E_out, IR_input[1], from_equal);
  and Z (Z_out, IR_input[0], from_zero);
  and and_17 (and_17_out, IR_input[4], IR_input[5], IR_input[6]);
  not not_1 (not_1_out, IR_input[3]);
  not not_2 (not_2_out, and_17_out);
  and and_18 (and_18_out, s_5, decoder_3x8_uc_1_out_5);
  and and_19 (and_19_out, s_5, decoder_3x8_uc_1_out_6);
  and and_20 (and_20_out, s_5, decoder_3x8_uc_1_out_7);
  and and_21 (and_21_out, s_5, decoder_3x8_uc_1_out_8);
  and and_22 (and_22_out, s_5, decoder_3x8_uc_1_out_10);
  and and_23 (and_23_out, s_5, decoder_3x8_uc_1_out_11);
  and and_24 (and_24_out, s_5, decoder_3x8_uc_1_out_13, not_1_out);
  or or_5 (or_5_out, C_out, A_out, E_out, Z_out);
  and and_25 (and_25_out, s_6, decoder_3x8_uc_1_out_5, not_2_out);
  and and_26 (and_26_out, s_6, decoder_3x8_uc_1_out_8);
  and and_27 (and_27_out, s_6, decoder_3x8_uc_1_out_11, or_5_out);
  or or_6 (or_6_out, s_1, and_11_out, and_14_out, and_9_out, and_10_out, and_13_out);
  or or_7 (or_7_out, s_3, and_12_out, and_22_out, and_23_out, and_26_out, and_27_out);
  or or_8 (or_8_out, and_18_out, and_15_out);
  or or_9 (or_9_out, and_19_out, and_25_out, and_21_out, and_24_out);
  and and_28 (IR_set, clk_s, s_2);
  and and_29 (to_MAR_s, or_6_out, clk_s);
  and and_30 (to_IAR_s, or_7_out, clk_s);
  or or_10 (or_10_out, s_1, and_11_out, and_14_out, and_18_out);
  and and_31 (to_ACC_s, or_10_out, clk_s);
  and and_32 (to_RAM_s, and_20_out, clk_s);
  and and_33 (to_TMP_s, clk_s, and_8_out);
  and and_34 (to_flag_s, clk_s, or_8_out);
  and and_35 (to_IO_s, clk_s, and_16_out);
  decoder2x4_UC decoder2x4_uc_1 (
    .in_3(IR_input[0]), .in_4(IR_input[1]), .in_1(or_9_out), .in_2(clk_s), .out_5(to_R0_s), .out_6(to_R1_s),
    .out_7(to_R2_s), .out_8(to_R3_s));

  assign Data_Adress = IR_input[2];
  assign Input_Output = IR_input[3];

  // Other names for the same wires on the sheet: from_IR[7:0] = IR_input; to_Flags_s = to_flag_s;
  //   to_ULA[2:0] = ULA_op

  // Notes on the sheet:
  //   IR
endmodule

module bus_1 (
  input  [7:0] in_1,
  input  in_2,
  output [7:0] out_3
);

  Multiplexer #(.width(8)) multiplexer_1 (.in0(in_1), .in1(8'h1), .out(out_3), .sel(in_2));
endmodule

module flag (
  input  in_1,
  input  in_2,
  input  in_3,
  input  in_4,
  input  in_5,
  output out_6,
  output out_7,
  output out_8,
  output out_9
);

  Register #(.width(4)) register_1 (
    .D({in_4, in_3, in_2, in_1}), .Q({out_9, out_8, out_7, out_6}), .clk(in_5));  // open: en, clr
endmodule

module dec4x8_UC (
  input  in_1,
  input  in_2,
  input  in_3,
  input  in_4,
  input  in_5,
  input  in_6,
  input  in_7,
  output out_8,
  output out_9,
  output out_10,
  output out_11
);

  wire and_1_out, and_2_out, and_3_out, and_4_out, and_5_out, and_6_out, and_7_out, and_8_out,
       decoder_1_out0, decoder_1_out1, decoder_1_out2, decoder_1_out3, decoder_2_out0, decoder_2_out1,
       decoder_2_out2, decoder_2_out3;

  or or_1 (out_8, and_5_out, and_1_out);
  or or_2 (out_9, and_6_out, and_2_out);
  or or_3 (out_10, and_7_out, and_3_out);
  or or_4 (out_11, and_8_out, and_4_out);
  and and_1 (and_1_out, in_1, in_2, decoder_1_out0);
  and and_2 (and_2_out, in_1, in_2, decoder_1_out1);
  and and_3 (and_3_out, in_1, in_2, decoder_1_out2);
  and and_4 (and_4_out, in_1, in_2, decoder_1_out3);
  and and_5 (and_5_out, in_1, in_3, decoder_2_out0);
  and and_6 (and_6_out, in_1, in_3, decoder_2_out1);
  and and_7 (and_7_out, in_1, in_3, decoder_2_out2);
  and and_8 (and_8_out, in_1, in_3, decoder_2_out3);
  Decoder #(.enable("false"), .select(2)) decoder_1 (
    .out0(decoder_1_out0), .out1(decoder_1_out1), .out2(decoder_1_out2), .out3(decoder_1_out3),
    .sel({in_5, in_4}));
  Decoder #(.enable("false"), .select(2)) decoder_2 (
    .out0(decoder_2_out0), .out1(decoder_2_out1), .out2(decoder_2_out2), .out3(decoder_2_out3),
    .sel({in_7, in_6}));
endmodule

module decoder2x4_UC (
  input  in_1,
  input  in_2,
  input  in_3,
  input  in_4,
  output out_5,
  output out_6,
  output out_7,
  output out_8
);

  wire decoder_1_out0, decoder_1_out1, decoder_1_out2, decoder_1_out3;

  Decoder #(.enable("false"), .select(2)) decoder_1 (
    .out0(decoder_1_out0), .out1(decoder_1_out1), .out2(decoder_1_out2), .out3(decoder_1_out3),
    .sel({in_4, in_3}));
  and and_1 (out_5, in_2, in_1, decoder_1_out0);
  and and_2 (out_6, in_2, in_1, decoder_1_out1);
  and and_3 (out_7, in_2, in_1, decoder_1_out2);
  and and_4 (out_8, in_2, in_1, decoder_1_out3);
endmodule

module decoder_3x8_UC (
  input  b7,
  input  b6,
  input  b5,
  input  b4,
  output out_5,
  output out_6,
  output out_7,
  output out_8,
  output out_9,
  output out_10,
  output out_11,
  output out_12,
  output out_13
);

  wire decoder_1_out0, decoder_1_out1, decoder_1_out2, decoder_1_out3, decoder_1_out4, decoder_1_out5,
       decoder_1_out6, decoder_1_out7, not_1_out;

  not not_1 (not_1_out, b7);
  Decoder #(.select(3)) decoder_1 (
    .out0(decoder_1_out0), .out1(decoder_1_out1), .out2(decoder_1_out2), .out3(decoder_1_out3),
    .out4(decoder_1_out4), .out5(decoder_1_out5), .out6(decoder_1_out6), .out7(decoder_1_out7),
    .sel({b6, b5, b4}));  // open: en
  and and_1 (out_6, not_1_out, decoder_1_out0);
  and and_2 (out_7, not_1_out, decoder_1_out1);
  and and_3 (out_8, not_1_out, decoder_1_out2);
  and and_4 (out_9, not_1_out, decoder_1_out3);
  and and_5 (out_10, not_1_out, decoder_1_out4);
  and and_6 (out_11, not_1_out, decoder_1_out5);
  and and_7 (out_12, not_1_out, decoder_1_out6);
  and and_8 (out_13, not_1_out, decoder_1_out7);

  assign out_5 = b7;
endmodule
